# Fritzing sketch mcopy_MONO_JK99_shield (saved by Fritzing 0.9.3b)
circuit board: 2.97497cm x 5.28509cm
breadboards: 1

parts:
  part = Arduino Uno (Rev3)
  part_2 = Screw terminal - 2 pins [package=THT]
  part_3 = Screw terminal - 2 pins [package=THT]
  part_4 = Screw terminal - 2 pins [package=THT]
  part_5 = Screw terminal - 2 pins [package=THT]

nets:
  N1: part.GND, part_3.pin2, part_5.pin1, part_5.pin2
  N2: part.D3_PWM, part_2.pin1
  N3: part.D4, part_2.pin2
  N4: part.D5_PWM, part_4.pin1
  N5: part.D6_PWM, part_4.pin2
  N6: part.5V, part_3.pin1

notes:
  proj adv [3]
  proj rew [4]
  takeup adv [5]
  takeup rew [6]
  [5V]
  [GND]
  mcopy JK99
